# Fritzing sketch sketch (saved by Fritzing 0.9.9b)
breadboards: 1

parts:
  Part1 = Arduino Uno (Rev3)
  M1 = LJ18A3-H-ZBX [package=THT]
  VCC1 = Battery block 9V
  U1 = 2-Channel 5v Relay Shield [package=relay-2ch5v10a]

nets:
  GND: Part1.GND, M1.VO_(BLU), VCC1.-, U1.GND
  N1: Part1.D2, M1.SIG_(BLK)
  N2: Part1.D3_PWM, U1.IN2
  5V: Part1.5V, U1.VCC
  N3: M1.VI_(BRN), VCC1.+

custom parts:
  LJ18A3-H-ZBX: LJ18A3-H-ZBX Proximity Sensor module.
  2-Channel 5v Relay Shield: 2 Channel 5v Relay Shield w. 2x SPD-06VDC-SD-C
